# Fritzing sketch Buzzer (saved by Fritzing 0.9.3b)
breadboards: 1

parts:
  BUZZER = Piezo Speaker
  Buzzer = Arduino Uno (Rev3)
  R1 = Resistor [tolerance=±5% resistance=220 package=THT]

nets:
  N1: BUZZER.pin1, Buzzer.GND
  N2: BUZZER.pin2, R1.Pin_0
  N3: Buzzer.D3_PWM, R1.Pin_1
