# Fritzing sketch LDR (saved by Fritzing 0.9.3b)
circuit board: 8.46667cm x 5.64444cm
breadboards: 1

parts:
  LDR = Arduino Uno (Rev3)
  LDR_2 = Photocell (LDR) [package=THT]
  R2 = Resistor [tolerance=±5% resistance=220 package=THT]

nets:
  N1: LDR.A2, LDR_2.pin_1, R2.Pin_0
  N2: LDR.GND, R2.Pin_1
  N3: LDR.5V, LDR_2.pin_0
