# Fritzing sketch WIFI (saved by Fritzing 0.9.3b)
breadboards: 1

parts:
  part = ESP8266 WiFi Module [part_number=ESP8266]
  Module_WIFI = Arduino Uno (Rev3)

nets:
  N1: part.RXD, Module_WIFI.D11_PWM/MOSI
  VCC: part.VCC, part.CH_PD, Module_WIFI.3V3
  GND: part.GND, Module_WIFI.GND
  N2: part.TXD, Module_WIFI.D10_PWM/SS

custom parts:
  ESP8266 WiFi Module: Generic WiFi Module based on the ESP8266 with onboard PCB antenna and UART communications
