# Fritzing sketch capteur de flamme (saved by Fritzing 0.9.3b)
breadboards: 1

parts:
  S1 = KY-026
  Capteur_flammes = Arduino Uno (Rev3)

nets:
  N1: S1.pin1, Capteur_flammes.A3
  N2: S1.pin2, Capteur_flammes.GND
  N3: S1.pin3, Capteur_flammes.5V

custom parts:
  KY-026: ky-026 flame sensor module
