# Fritzing sketch dht (saved by Fritzing 0.9.3b)
circuit board: 8.46667cm x 5.64444cm
breadboards: 1

parts:
  DHT11_externe = DHT11 module
  DHT11_interne = DHT11 module
  Composant1 = Arduino Uno (Rev3)

nets:
  VCC: DHT11_externe.VCC, DHT11_interne.VCC, Composant1.5V
  GND: DHT11_externe.GND, DHT11_interne.GND, Composant1.GND

custom parts:
  DHT11 module: DHT11 black pcb module
