# Fritzing sketch fin d course 2 (saved by Fritzing 0.9.3b)
breadboards: 1

parts:
  R1 = Resistor [tolerance=±5% resistance=220 package=THT]
  D2F1 = D2F-FL Omron Snap Action Limit Switch with Level
  Fin-course-Toit = Arduino Uno (Rev3)

nets:
  N1: R1.Pin_0, D2F1.COM, Fin-course-Toit.A4/SDA
  N2: R1.Pin_1, Fin-course-Toit.GND
  N3: D2F1.NC, Fin-course-Toit.5V

custom parts:
  D2F-FL Omron Snap Action Limit Switch with Level: Snap action switch with stainless steel lever.
